# Fritzing sketch LED_D3 (saved by Fritzing 0.9.4)
breadboards: 1

parts:
  Part1 = Arduino Uno (Rev3) - ICSP
  LED_Cathode_(-)_is_on_left_(flat_side_and_shorter_lead)_LED_Anode_(+)_is_on_right = LED - 5mm [color="Red (633nm)" package="5 mm [THT]"]
  Resistor = Resistor [tolerance=±5% resistance=330 package=THT]

nets:
  N1: Part1.GND, LED_Cathode_(-)_is_on_left_(flat_side_and_shorter_lead)_LED_Anode_(+)_is_on_right.cathode
  N2: Part1.D3_PWM, Resistor.Pin_1
  N3: LED_Cathode_(-)_is_on_left_(flat_side_and_shorter_lead)_LED_Anode_(+)_is_on_right.anode, Resistor.Pin_0
