# Fritzing sketch LED_D3_Pot_A0 (saved by Fritzing 0.9.4)
breadboards: 1

parts:
  Part1 = Arduino Uno (Rev3) - ICSP
  LED_Cathode_(-)_is_on_left_(flat_side_and_shorter_lead)_LED_Anode_(+)_is_on_right = LED - 5mm [color="Red (633nm)" package="5 mm [THT]"]
  Resistor = Resistor [tolerance=±5% resistance=330 package=THT]
  R1 = Rotary Potentiometer (Small) [maximum_resistance=100kΩ package=THT]

nets:
  N1: Part1.A0, R1.wiper
  N2: Part1.GND, LED_Cathode_(-)_is_on_left_(flat_side_and_shorter_lead)_LED_Anode_(+)_is_on_right.cathode, R1.leg1
  N3: Part1.D3_PWM, Resistor.Pin_1
  N4: Part1.5V, R1.leg2
  N5: LED_Cathode_(-)_is_on_left_(flat_side_and_shorter_lead)_LED_Anode_(+)_is_on_right.anode, Resistor.Pin_0
